// Digital circuit lab01.dig as structural Verilog
module lab01 (
  input  clk
);

  wire u_gen_tick_tick;

  gen_tick #(.applicationType("IVERILOG"), .CodeFile("C:\\Users\\Meta_\\Downloads\\gen_tick.v")) u_gen_tick (
    .src_clk(clk), .enable(clk), .tick(u_gen_tick_tick));
  LED led_1 (.in(u_gen_tick_tick));
  // also tied to VCC on the sheet: clk

  // Notes on the sheet:
  //   clk: Hz: 5000
endmodule
